// Logisim project CARRINHO+CONTAGEM+TEMPO.circ as structural Verilog: 1 circuit, main circuit main
module main (
  input  M,
  input  a,
  input  b,
  output M1,
  output VAL,
  output M2,
  output HABILITA,
  output _512Hz,
  output _256Hz,
  output _128Hz,
  output _64Hz,
  output _32Hz,
  output _16Hz,
  output _8Hz,
  output _2Hz,
  output _1Hz,
  output _1,
  output _2,
  output _4,
  output _8,
  output out_21,
  output out_22,
  output out_23,
  output out_24
);

  wire _1KHz_out, and_1_out, and_2_out, and_3_out, and_4_out, and_5_out, and_6_out, and_7_out, and_8_out,
       and_9_out, and_10_out, and_11_out, and_12_out, E0_q, FLAG_5_out, FS_out, not_1_out, or_1_out,
       or_2_out, or_3_out, or_4_out, or_5_out, or_6_out, or_7_out, or_8_out, or_9_out, T01_out, T12_out,
       T23_out, T30_1_out, T30_out;

  and FLAG_5 (FLAG_5_out, ~_8, _4, ~_2, _1);  // AND_Gate
  and T01 (T01_out, E0_q, M, a);
  and T12 (T12_out, M1, b);
  and T23 (T23_out, HABILITA, FLAG_5_out);
  and T30 (T30_out, M2, a);
  and FS (FS_out, ~E0_q, ~M1, ~HABILITA, ~M2);  // AND_Gate
  not not_1 (not_1_out, _1KHz_out);
  Clock _1KHz (.out(_1KHz_out));
  or T30_1 (T30_1_out, T30_out, FS_out);
  J_K_Flip_Flop j_k_ff_1 (.J(HABILITA), .clk(not_1_out), .K(HABILITA), .Q(_512Hz));  // open: Qn, preset, en, reset
  J_K_Flip_Flop j_k_ff_2 (.J(HABILITA), .clk(_64Hz), .K(HABILITA), .Q(_32Hz));  // open: Qn, preset, en, reset
  J_K_Flip_Flop j_k_ff_3 (.J(HABILITA), .clk(_1Hz), .K(HABILITA), .Q(_1), .reset(or_9_out));  // open: Qn, preset, en
  J_K_Flip_Flop E0 (.Q(E0_q), .preset(T30_1_out), .reset(T01_out));  // open: J, clk, K, Qn, en
  J_K_Flip_Flop E1 (.Q(M1), .preset(T01_out), .reset(T12_out));  // open: J, clk, K, Qn, en
  J_K_Flip_Flop E2 (.Q(HABILITA), .preset(T12_out), .reset(T23_out));  // open: J, clk, K, Qn, en
  J_K_Flip_Flop E3 (.Q(M2), .preset(T23_out), .reset(T30_1_out));  // open: J, clk, K, Qn, en
  and and_1 (and_1_out, ~_4, ~_1);  // AND_Gate
  and and_2 (and_2_out, _4, _1);
  and and_3 (and_3_out, ~_2, ~_1);  // AND_Gate
  and and_4 (and_4_out, _2, _1);
  and and_5 (and_5_out, ~_4, _2);  // AND_Gate
  and and_6 (and_6_out, _2, ~_1);  // AND_Gate
  and and_7 (and_7_out, _4, ~_2, _1);  // AND_Gate
  and and_8 (and_8_out, _4, ~_2);  // AND_Gate
  and and_9 (and_9_out, _4, ~_1);  // AND_Gate
  J_K_Flip_Flop j_k_ff_4 (.J(HABILITA), .clk(_512Hz), .K(HABILITA), .Q(_256Hz));  // open: Qn, preset, en, reset
  J_K_Flip_Flop j_k_ff_5 (.J(HABILITA), .clk(_32Hz), .K(HABILITA), .Q(_16Hz));  // open: Qn, preset, en, reset
  J_K_Flip_Flop j_k_ff_6 (.J(_1), .clk(_1Hz), .K(_1), .Q(_2), .reset(or_9_out));  // open: Qn, preset, en
  or or_1 (or_1_out, and_1_out, and_5_out, and_6_out, and_7_out);
  J_K_Flip_Flop j_k_ff_7 (.J(HABILITA), .clk(_256Hz), .K(HABILITA), .Q(_128Hz));  // open: Qn, preset, en, reset
  J_K_Flip_Flop j_k_ff_8 (.J(HABILITA), .clk(_16Hz), .K(HABILITA), .Q(_8Hz));  // open: Qn, preset, en, reset
  and and_10 (and_10_out, _1, _2);
  J_K_Flip_Flop j_k_ff_9 (
    .J(and_10_out), .clk(_1Hz), .K(and_10_out), .Q(_4), .reset(or_9_out));  // open: Qn, preset, en
  or or_2 (or_2_out, _8, _2, and_1_out, and_2_out);
  or or_3 (or_3_out, ~_4, and_3_out, and_4_out);  // OR_Gate
  or or_4 (or_4_out, _4, ~_2, _1);  // OR_Gate
  or or_5 (or_5_out, _8, or_1_out);
  or or_6 (or_6_out, and_1_out, and_6_out);
  or or_7 (or_7_out, and_3_out, and_8_out, and_9_out, _8);
  or or_8 (or_8_out, and_8_out, and_9_out, and_5_out, _8);
  _7_Segment_Display u_7_segment_display_1 (
    .g(or_8_out), .f(or_7_out), .a(or_2_out), .b(or_3_out), .e(or_6_out), .d(or_5_out), .c(or_4_out));  // open: dp
  J_K_Flip_Flop j_k_ff_10 (.J(HABILITA), .clk(_128Hz), .K(HABILITA), .Q(_64Hz));  // open: Qn, preset, en, reset
  J_K_Flip_Flop j_k_ff_11 (.J(HABILITA), .clk(_8Hz), .K(HABILITA), .Q(_2Hz));  // open: Qn, preset, en, reset
  J_K_Flip_Flop j_k_ff_12 (.J(HABILITA), .clk(_2Hz), .K(HABILITA), .Q(_1Hz));  // open: Qn, preset, en, reset
  and and_11 (and_11_out, and_10_out, _4);
  J_K_Flip_Flop j_k_ff_13 (
    .J(and_11_out), .clk(_1Hz), .K(and_11_out), .Q(_8), .reset(or_9_out));  // open: Qn, preset, en
  or or_9 (or_9_out, E0_q, and_12_out);
  and and_12 (and_12_out, ~_1, _2, ~_4, _8);  // AND_Gate

  assign out_21 = _1;
  assign out_22 = _2;
  assign out_23 = _4;
  assign out_24 = _8;
  assign VAL = HABILITA;

  // Notes on the sheet:
  //   B                           C                      D                   8  4  2  1
  //   TEMPORIZADOR
  //   RESET PARA 10
endmodule
