// Logisim project TrabCircBCD.circ as structural Verilog: 1 circuit, main circuit main
module main (
  input  A,
  input  B,
  input  C,
  input  D,
  input  in_5,
  input  in_6,
  input  in_7,
  input  in_8,
  input  A_2,
  input  B_2,
  input  C_2,
  input  D_2,
  output out_13,
  output out_14,
  output out_15
);

  wire and_1_out, and_2_out, nand_1_out, nand_2_out, nand_3_out, nand_4_out, nand_5_out, nand_6_out,
       nor_1_out, nor_2_out, nor_4_out, nor_6_out, not_1_out, not_2_out, not_3_out, or_1_out, xor_1_out;

  not not_1 (not_1_out, A_2);
  not not_2 (not_2_out, B);
  not not_3 (not_3_out, C_2);
  nor nor_1 (nor_1_out, A, B);
  nand nand_1 (nand_1_out, A, C);
  nand nand_2 (nand_2_out, not_2_out, D);
  and and_1 (and_1_out, nor_1_out, nand_1_out);
  xor xor_1 (xor_1_out, B_2, B_2);
  nand nand_3 (nand_3_out, A_2, not_3_out, D_2);
  nor nor_2 (nor_2_out, not_1_out, B_2, not_3_out);
  nor nor_3 (out_14, and_1_out, nand_2_out);
  and and_2 (and_2_out, C_2, nor_4_out);
  nor nor_4 (nor_4_out, nand_3_out, nor_2_out);
  nand nand_4 (nand_4_out, nor_2_out, D_2);
  nor nor_5 (out_15, xor_1_out, and_2_out, nand_4_out);
  nand nand_5 (nand_5_out, ~in_5, in_6);  // NAND_Gate
  nand nand_6 (nand_6_out, in_5, ~in_6);  // NAND_Gate
  nor nor_6 (nor_6_out, in_7, in_8);
  or or_1 (or_1_out, nand_5_out, nand_6_out, in_7);
  and and_3 (out_13, or_1_out, nor_6_out);
endmodule
