// Logisim project Trabalho Carrinho(16-11-2015).circ as structural Verilog: 1 circuit, main circuit main
module main (
  input  BT_L,
  input  FCA,
  input  FCB,
  input  Bal_100kg,
  output CARRINHO,
  output Move_p__direita,
  output \Válvula_A ,
  output Move_p__esquerda
);

  wire E0_q, FS_out, or_1_out, T01_out, T12_out, T23_out, T30_out;

  and T01 (T01_out, BT_L, E0_q, FCA);
  and T12 (T12_out, FCB, Move_p__direita);
  and T23 (T23_out, Bal_100kg, \Válvula_A );
  and T30 (T30_out, FCA, Move_p__esquerda);
  and FS (FS_out, ~E0_q, ~Move_p__direita, ~\Válvula_A , ~Move_p__esquerda);  // AND_Gate
  or or_1 (or_1_out, T30_out, FS_out);
  J_K_Flip_Flop E0 (.Q(E0_q), .preset(or_1_out), .reset(T01_out));  // open: J, clk, K, Qn, en
  J_K_Flip_Flop E1 (.Q(Move_p__direita), .preset(T01_out), .reset(T12_out));  // open: J, clk, K, Qn, en
  J_K_Flip_Flop E2 (.Q(\Válvula_A ), .preset(T12_out), .reset(T23_out));  // open: J, clk, K, Qn, en
  J_K_Flip_Flop E3 (.Q(Move_p__esquerda), .preset(T23_out), .reset(or_1_out));  // open: J, clk, K, Qn, en
  or or_2 (CARRINHO, Move_p__direita, Move_p__esquerda);

  // Notes on the sheet:
  //   CARRINHO
endmodule
