// Logisim project Trabalho Eletrólise (14-11-2015).circ as structural Verilog: 1 circuit, main circuit main
module main (
  input  PTD,
  input  F2,
  input  F3,
  input  F4,
  input  F5,
  input  F6,
  input  F7,
  output M2_Sobe,
  output \M1_Avança ,
  output M2_Desce,
  output M1_Retorna
);

  wire E0_q, E1_q, E2_q, E3_q, E4_q, E5_q, E6_q, E7_q, E8_q, E9_q, E10_q, E12_q, FS_out, or_1_out, T01_out,
       T12_out, T23_out, T34_out, T45_out, T56_out, T67_out, T78_out, T89_out, T120_out, T910_out, T1011_out,
       T1112_out;

  and T01 (T01_out, PTD, F2, F7, E0_q);
  and T12 (T12_out, F3, F7, E1_q);
  and T23 (T23_out, F3, F4, E2_q);
  and T34 (T34_out, F2, F4, E3_q);
  and T45 (T45_out, F3, F4, E4_q);
  and T56 (T56_out, F3, F5, E5_q);
  and T67 (T67_out, F2, F5, E6_q);
  and T78 (T78_out, F3, F5, E7_q);
  and T89 (T89_out, F3, F6, E8_q);
  and T910 (T910_out, F2, F6, E9_q);
  and T1011 (T1011_out, F3, F6, E10_q);
  and T1112 (T1112_out, F7, F3, M1_Retorna);
  and T120 (T120_out, F7, F2, E12_q);
  and FS (FS_out, ~E0_q, ~E1_q, ~E2_q, ~E3_q, ~E4_q, ~E5_q, ~E6_q, ~E7_q, ~E8_q, ~E9_q, ~E10_q, ~M1_Retorna, ~E12_q);  // AND_Gate
  or or_1 (or_1_out, T120_out, FS_out);
  J_K_Flip_Flop E0 (.Q(E0_q), .preset(or_1_out), .reset(T01_out));  // open: J, clk, K, Qn, en
  J_K_Flip_Flop E1 (.Q(E1_q), .preset(T01_out), .reset(T12_out));  // open: J, clk, K, Qn, en
  J_K_Flip_Flop E2 (.Q(E2_q), .preset(T12_out), .reset(T23_out));  // open: J, clk, K, Qn, en
  J_K_Flip_Flop E3 (.Q(E3_q), .preset(T23_out), .reset(T34_out));  // open: J, clk, K, Qn, en
  J_K_Flip_Flop E4 (.Q(E4_q), .preset(T34_out), .reset(T45_out));  // open: J, clk, K, Qn, en
  J_K_Flip_Flop E5 (.Q(E5_q), .preset(T45_out), .reset(T56_out));  // open: J, clk, K, Qn, en
  J_K_Flip_Flop E6 (.Q(E6_q), .preset(T56_out), .reset(T67_out));  // open: J, clk, K, Qn, en
  J_K_Flip_Flop E7 (.Q(E7_q), .preset(T67_out), .reset(T78_out));  // open: J, clk, K, Qn, en
  J_K_Flip_Flop E8 (.Q(E8_q), .preset(T78_out), .reset(T89_out));  // open: J, clk, K, Qn, en
  J_K_Flip_Flop E9 (.Q(E9_q), .preset(T89_out), .reset(T910_out));  // open: J, clk, K, Qn, en
  J_K_Flip_Flop E10 (.Q(E10_q), .preset(T910_out), .reset(T1011_out));  // open: J, clk, K, Qn, en
  J_K_Flip_Flop E11 (.Q(M1_Retorna), .preset(T1011_out), .reset(T1112_out));  // open: J, clk, K, Qn, en
  J_K_Flip_Flop E12 (.Q(E12_q), .preset(T1112_out), .reset(or_1_out));  // open: J, clk, K, Qn, en
  or or_2 (M2_Sobe, E1_q, E10_q, E7_q, E4_q);
  or or_3 (\M1_Avança , E2_q, E8_q, E5_q);
  or or_4 (M2_Desce, E3_q, E12_q, E9_q, E6_q);

  // Notes on the sheet:
  //   Processo de Eletrólise
  //   Rafael F. Ferreira
  //   1º Ano - C.C. Unespar
endmodule
