// Logisim project Trabalho Partida Compensadora - Rafael Francisco Ferreira.circ as structural Verilog: 1 circuit, main circuit main
module main (
  input  BT_LD,
  input  BT_LE,
  input  BT_DES,
  output C1,
  output C2,
  output C3,
  output C4,
  output C5,
  output HABILITA,
  output _512Hz,
  output _256Hz,
  output _128Hz,
  output _64Hz,
  output _32Hz,
  output _16Hz,
  output _8Hz,
  output _2Hz,
  output _1Hz,
  output _1,
  output _2,
  output _4,
  output _8,
  output out_23,
  output out_24,
  output out_25,
  output out_26
);

  wire _1KHz_out, and_1_out, and_2_out, and_3_out, and_4_out, and_5_out, and_6_out, and_7_out, and_13_out,
       and_14_out, and_15_out, and_16_out, and_17_out, and_18_out, and_19_out, and_20_out, and_21_out,
       and_22_out, and_23_out, and_24_out, FLAG_5_out, FS_out, j_k_ff_1_q, j_k_ff_2_q, j_k_ff_3_q,
       j_k_ff_4_q, j_k_ff_5_q, j_k_ff_6_q, not_1_out, not_2_out, not_3_out, or_1_out, or_2_out, or_3_out,
       or_4_out, or_5_out, or_6_out, or_8_out, or_9_out, or_10_out, or_11_out, or_12_out, or_13_out,
       or_14_out, or_15_out, or_16_out, STBY_q;

  not not_1 (not_1_out, BT_LD);
  not not_2 (not_2_out, BT_LE);
  or or_1 (or_1_out, j_k_ff_4_q, j_k_ff_5_q, and_1_out);
  and and_1 (and_1_out, STBY_q, BT_LD);
  and and_2 (and_2_out, ~j_k_ff_1_q, BT_LD, FLAG_5_out);  // AND_Gate
  and and_3 (and_3_out, ~j_k_ff_2_q, and_7_out);  // AND_Gate
  and and_4 (and_4_out, STBY_q, BT_LE);
  and and_5 (and_5_out, ~j_k_ff_4_q, BT_LE, FLAG_5_out);  // AND_Gate
  and and_6 (and_6_out, ~j_k_ff_5_q, and_7_out);  // AND_Gate
  and FS (FS_out, ~BT_LD, ~BT_LE, ~BT_DES);  // AND_Gate
  J_K_Flip_Flop STBY (.Q(STBY_q), .preset(FS_out), .reset(or_1_out));  // open: J, clk, K, Qn, en
  J_K_Flip_Flop j_k_ff_1 (.Q(j_k_ff_1_q), .preset(and_1_out), .reset(FLAG_5_out));  // open: J, clk, K, Qn, en
  J_K_Flip_Flop j_k_ff_2 (.Q(j_k_ff_2_q), .preset(and_2_out), .reset(and_7_out));  // open: J, clk, K, Qn, en
  J_K_Flip_Flop j_k_ff_3 (.Q(j_k_ff_3_q), .preset(and_3_out), .reset(not_1_out));  // open: J, clk, K, Qn, en
  J_K_Flip_Flop j_k_ff_4 (.Q(j_k_ff_4_q), .preset(and_4_out), .reset(FLAG_5_out));  // open: J, clk, K, Qn, en
  J_K_Flip_Flop j_k_ff_5 (.Q(j_k_ff_5_q), .preset(and_5_out), .reset(and_7_out));  // open: J, clk, K, Qn, en
  J_K_Flip_Flop j_k_ff_6 (.Q(j_k_ff_6_q), .preset(and_6_out), .reset(not_2_out));  // open: J, clk, K, Qn, en
  and and_7 (and_7_out, ~_8, _4, _2, ~_1);  // AND_Gate
  or or_2 (or_2_out, j_k_ff_6_q, j_k_ff_2_q, j_k_ff_3_q);
  or or_3 (or_3_out, j_k_ff_4_q, j_k_ff_1_q, j_k_ff_4_q);
  or or_4 (or_4_out, j_k_ff_4_q, j_k_ff_1_q, j_k_ff_4_q);
  or or_5 (or_5_out, j_k_ff_5_q, j_k_ff_4_q, j_k_ff_6_q);
  or or_6 (or_6_out, j_k_ff_1_q, j_k_ff_3_q, j_k_ff_2_q);
  and and_8 (C1, ~BT_DES, or_2_out);  // AND_Gate
  and and_9 (C2, ~BT_DES, or_3_out);  // AND_Gate
  and and_10 (C3, or_4_out, ~BT_DES);  // AND_Gate
  and and_11 (C4, or_5_out, ~BT_DES);  // AND_Gate
  and and_12 (C5, or_6_out, ~BT_DES);  // AND_Gate
  and FLAG_5 (FLAG_5_out, ~_8, _4, ~_2, _1);  // AND_Gate
  Clock _1KHz (.out(_1KHz_out));
  or or_7 (HABILITA, j_k_ff_5_q, j_k_ff_2_q, j_k_ff_1_q, j_k_ff_4_q);
  not not_3 (not_3_out, _1KHz_out);
  _7_Segment_Display u_7_segment_display_1 (
    .g(or_15_out), .f(or_14_out), .a(or_9_out), .b(or_10_out), .e(or_13_out), .d(or_12_out), .c(or_11_out));  // open: dp
  J_K_Flip_Flop j_k_ff_7 (.J(HABILITA), .clk(not_3_out), .K(HABILITA), .Q(_512Hz));  // open: Qn, preset, en, reset
  J_K_Flip_Flop j_k_ff_8 (.J(HABILITA), .clk(_64Hz), .K(HABILITA), .Q(_32Hz));  // open: Qn, preset, en, reset
  J_K_Flip_Flop j_k_ff_9 (.J(HABILITA), .clk(_1Hz), .K(HABILITA), .Q(_1), .reset(or_16_out));  // open: Qn, preset, en
  and and_13 (and_13_out, ~_4, ~_1);  // AND_Gate
  and and_14 (and_14_out, _4, _1);
  and and_15 (and_15_out, ~_2, ~_1);  // AND_Gate
  and and_16 (and_16_out, _2, _1);
  and and_17 (and_17_out, ~_4, _2);  // AND_Gate
  and and_18 (and_18_out, _2, ~_1);  // AND_Gate
  and and_19 (and_19_out, _4, ~_2, _1);  // AND_Gate
  and and_20 (and_20_out, _4, ~_2);  // AND_Gate
  and and_21 (and_21_out, _4, ~_1);  // AND_Gate
  J_K_Flip_Flop j_k_ff_10 (.J(HABILITA), .clk(_512Hz), .K(HABILITA), .Q(_256Hz));  // open: Qn, preset, en, reset
  J_K_Flip_Flop j_k_ff_11 (.J(HABILITA), .clk(_32Hz), .K(HABILITA), .Q(_16Hz));  // open: Qn, preset, en, reset
  J_K_Flip_Flop j_k_ff_12 (.J(_1), .clk(_1Hz), .K(_1), .Q(_2), .reset(or_16_out));  // open: Qn, preset, en
  or or_8 (or_8_out, and_13_out, and_17_out, and_18_out, and_19_out);
  J_K_Flip_Flop j_k_ff_13 (.J(HABILITA), .clk(_256Hz), .K(HABILITA), .Q(_128Hz));  // open: Qn, preset, en, reset
  J_K_Flip_Flop j_k_ff_14 (.J(HABILITA), .clk(_16Hz), .K(HABILITA), .Q(_8Hz));  // open: Qn, preset, en, reset
  and and_22 (and_22_out, _1, _2);
  or or_9 (or_9_out, _8, _2, and_13_out, and_14_out);
  or or_10 (or_10_out, ~_4, and_15_out, and_16_out);  // OR_Gate
  or or_11 (or_11_out, _4, ~_2, _1);  // OR_Gate
  or or_12 (or_12_out, _8, or_8_out);
  or or_13 (or_13_out, and_13_out, and_18_out);
  or or_14 (or_14_out, and_15_out, and_20_out, and_21_out, _8);
  or or_15 (or_15_out, and_20_out, and_21_out, and_17_out, _8);
  J_K_Flip_Flop j_k_ff_15 (.J(HABILITA), .clk(_128Hz), .K(HABILITA), .Q(_64Hz));  // open: Qn, preset, en, reset
  J_K_Flip_Flop j_k_ff_16 (.J(HABILITA), .clk(_8Hz), .K(HABILITA), .Q(_2Hz));  // open: Qn, preset, en, reset
  J_K_Flip_Flop j_k_ff_17 (
    .J(and_22_out), .clk(_1Hz), .K(and_22_out), .Q(_4), .reset(or_16_out));  // open: Qn, preset, en
  J_K_Flip_Flop j_k_ff_18 (.J(HABILITA), .clk(_2Hz), .K(HABILITA), .Q(_1Hz));  // open: Qn, preset, en, reset
  and and_23 (and_23_out, and_22_out, _4);
  J_K_Flip_Flop j_k_ff_19 (
    .J(and_23_out), .clk(_1Hz), .K(and_23_out), .Q(_8), .reset(or_16_out));  // open: Qn, preset, en
  or or_16 (or_16_out, BT_DES, and_24_out);
  and and_24 (and_24_out, ~_1, _2, ~_4, _8);  // AND_Gate

  assign out_23 = _1;
  assign out_24 = _2;
  assign out_25 = _4;
  assign out_26 = _8;

  // Notes on the sheet:
  //   RAFAEL FRANCISCO FERREIRA - 1º Ano C.C Unespar
  //   B                           C                      D                   8  4  2  1
endmodule
